# Fritzing sketch hackathon_fritzing_V2 (saved by Fritzing 0.9.3b)
circuit board: 8.46667cm x 5.64444cm
breadboards: 2

parts:
  Onderdeel1 = Arduino Mega ADK (Rev3)
  S1 = SWITCH-MOMENTARY-2 [package=tactile-pth]
  S2 = SWITCH-MOMENTARY-2 [package=tactile-pth]
  S3 = SWITCH-MOMENTARY-2 [package=tactile-pth]
  LED1 = LEDs [package=led10mm]
  LED2 = LEDs [package=led10mm]
  LED3 = LEDs [package=led10mm]
  LED4 = LEDs [package=led10mm]
  LED5 = LEDs [package=led10mm]
  LED6 = LEDs [package=led10mm]
  Onderdeel2 = Arduino Nano (Rev3.0) (ICSP)
  Grove1 = Grove 4 Digit Display
  D1 = LED_BARGRAPH_10 [package=led_bargaph_10]  # not connected
  Onderdeel3 = 16 NeoPixel Ring [part_number=1463]
  U1 = POT [package=pot_alpha_rv16af-20]
  Onderdeel4 = Adafruit VL530X Time of Flight Distance Sensor [part_number="Adafruit #3317"]
  Mod1 = AK-FST 433mhz transmitter [package=THT]
  IR1 = TSOP312.., 314.. [package=THT]

nets:
  N1: Onderdeel1.A15, U1.S
  N2: Onderdeel1.A2, Onderdeel2.A2
  N3: Onderdeel1.A3, Onderdeel2.A3
  N4: Onderdeel1.D21/SCL, Onderdeel4.SCL
  N5: Onderdeel1.D20/SDA, Onderdeel4.SDA
  GND: Onderdeel1.GND, Onderdeel3.GND, U1.A
  N6: Onderdeel1.D13_PWM, LED1.C
  N7: Onderdeel1.D12_PWM, LED6.C
  N8: Onderdeel1.D11_PWM, LED5.C
  N9: Onderdeel1.D10_PWM, LED4.C
  N10: Onderdeel1.D9_PWM, LED3.C
  N11: Onderdeel1.D8_PWM, LED2.C
  5V: Onderdeel1.5V, Onderdeel4.VCC
  VIN: Onderdeel1.VIN, Onderdeel3.VDD, U1.E
  N12: Onderdeel1.D2_PWM, IR1.Data
  N13: Onderdeel1.D5_PWM, S1.2
  N14: Onderdeel1.D6_PWM, S2.2
  N15: Onderdeel1.D7_PWM, S3.2
  N16: Onderdeel1.D22, Mod1.pin3
  N17: Onderdeel1.D33, Onderdeel3.OUT
  N18: S1.1, S2.1, S3.1
  N19: Onderdeel2.D3, Grove1.DIO
  N20: Onderdeel2.D5, Grove1.CLK
  VIN_2: Onderdeel2.VIN, Grove1.VCC
  GND_2: Onderdeel2.GND, Grove1.GND
  N21: Onderdeel4.GND, Mod1.pin2
  N22: Mod1.pin4, IR1.Vs

notes:
  IR INPUT SIGNAL (grijs)
  INPUT SEQUENCE (zwart
  DR BIBBER (paars)
  TOF (roanje)
  CONNECT THE WIRES (wit)
  Draaislot (GROEN)
  tx voor shock collar
  TOF sensor
  IR RECIEVER

custom parts:
  16 NeoPixel Ring: 16 ultra bright smart LED NeoPixels are arranged in a circle with 1.75" (44.5mm) outer diameter. The rings are 'chainable' - connect the output pin of one to the input pin of another. Use only one microcontroller pin to control as many as you can chain together! Each LED is addressable as the driver chip is inside the LED. Each one has ~18mA constant current drive so the color will be very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
  Adafruit VL530X Time of Flight Distance Sensor: The VL53L0X is a Time of Flight distance sensor like no other you've used! The sensor contains a very tiny invisible laser source, and a matching sensor. The VL53L0X can detect the "time of flight", or how long the light has taken to bounce back to the sensor. Since it uses a very narrow light source, it is good for determining distance of only the surface directly in front of it. Unlike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
  AK-FST 433mhz transmitter: AK-FST 433mhz transmitter.
